// Logisim project Control Unit.circ as structural Verilog: 4 circuits, main circuit main
module main (
  input  Este_bit_me_lo_pasa_el_instruction_decoder,
  input  Reloj,
  input  Start,
  input  Reset,
  input  [1:0] operacion,
  input  [3:0] Read_Time,
  input  [3:0] Write_Time
);

  wire d_ff_1_q, demultiplexer_1_out0, demultiplexer_1_out1, demultiplexer_2_out0, demultiplexer_2_out1,
       Insruction_Read_q, Leer, Load_PC0, or_1_out, or_2_out, R_W_RF0;

  D_Flip_Flop d_ff_1 (.clk(Reloj), .D(demultiplexer_1_out0), .Q(d_ff_1_q));  // open: Qn, preset, en, reset
  buf or_1 (or_1_out, d_ff_1_q);  // OR_Gate
  Demultiplexer #(.enable("false")) demultiplexer_1 (
    .out0(demultiplexer_1_out0), .out1(demultiplexer_1_out1), .in(or_1_out), .sel(Start));
  D_Flip_Flop #(.trigger("falling")) Insruction_Read (
    .clk(Reloj), .D(or_2_out), .Q(Insruction_Read_q), .reset(Reset));  // open: Qn, preset, en
  or or_2 (or_2_out, demultiplexer_1_out1, demultiplexer_2_out0);
  Contador_de_Ciclos contador_de_ciclos_1 (
    .Read_Time(Read_Time), .Write_Time(Write_Time), .Reloj(Reloj),
    .R_W(Este_bit_me_lo_pasa_el_instruction_decoder), .Leido(Leer));  // open: Escrito
  Demultiplexer #(.enable("false")) demultiplexer_2 (
    .out0(demultiplexer_2_out0), .out1(demultiplexer_2_out1), .in(Insruction_Read_q), .sel(Leer));
  Demultiplexer #(.select(2), .enable("false")) demultiplexer_3 (
    .out0(Load_PC0), .out1(R_W_RF0), .in(demultiplexer_2_out1), .sel(operacion));  // open: out2, out3

  // Other names for the same wires on the sheet: CLK = Reloj; Op[1:0] = operacion; Read_Tm[3:0] = Read_Time;
  //   Resert = Reset; Write_Tm[3:0] = Write_Time

  // Notes on the sheet:
  //   Reloj
  //   Selector de Operacion
  //   INDLE
  //   (se lo pasa el instruction Decoder)
  //   Control Unit
  //   Cargar info de la RAM
  //   Contador de ciclos
  //   Jmp, nor, Jr
  //   Alu (Tipo R and Tipo I)
endmodule

module Registro_de_Instrucciones (
  input  [31:0] Ram_Out_0,
  input  [31:0] Ram_Out_1,
  input  [31:0] Ram_Out_2,
  input  [31:0] Ram_Out_3,
  input  [1:0] Select_Instruction,
  input  Reloj,
  input  En,
  input  Reset,
  output [31:0] out_9
);

  wire [31:0] Instruction_0, Instruction_1, Instruction_2, Instruction_3;

  Register #(.width(32)) register_1 (.D(Ram_Out_0), .en(Reloj), .Q(Instruction_0), .clk(En), .clr(Reset));
  Register #(.width(32)) register_2 (.D(Ram_Out_1), .en(Reloj), .Q(Instruction_1), .clk(En), .clr(Reset));
  Register #(.width(32)) register_3 (.D(Ram_Out_2), .en(Reloj), .Q(Instruction_2), .clk(En), .clr(Reset));
  Register #(.width(32)) register_4 (.D(Ram_Out_3), .en(Reloj), .Q(Instruction_3), .clk(En), .clr(Reset));
  Multiplexer #(.select(2), .width(32), .enable("false")) multiplexer_1 (
    .in0(Instruction_0), .in1(Instruction_1), .in2(Instruction_2), .in3(Instruction_3), .out(out_9),
    .sel(Select_Instruction));

  // Other names for the same wires on the sheet: CLK = Reloj; Instruc[1:0] = Select_Instruction

  // Notes on the sheet:
  //   Data From Ram
  //   Selector de Instruccion
  //   Cosas de los Registro
  //   Out
endmodule

module Contador_de_Ciclos (
  input  [3:0] Read_Time,
  input  [3:0] Write_Time,
  input  Reloj,
  input  R_W,
  output Leido,
  output Escrito
);

  wire comparator_1_eq;
  wire [3:0] multiplexer_1_out, Registro_Contador_q, Time;

  Counter #(.width(4), .max('hf)) Registro_Contador (
    .Q(Registro_Contador_q), .clk(Reloj));  // open: load, D, count, carry, clr
  Multiplexer #(.width(4), .enable("false")) multiplexer_1 (
    .in0(Read_Time), .in1(Write_Time), .out(multiplexer_1_out), .sel(R_W));
  Demultiplexer #(.enable("false")) demultiplexer_1 (.out0(Leido), .out1(Escrito), .in(comparator_1_eq), .sel(R_W));
  Comparator #(.width(4), .mode("unsigned")) comparator_1 (
    .a(Registro_Contador_q), .b(Time), .eq(comparator_1_eq));  // open: gt, lt
  Adder #(.width(4)) adder_1 (.a(multiplexer_1_out), .b(4'b0001), .out(Time));  // open: cin, cout

  // Other names for the same wires on the sheet: CLK = Reloj

  // Notes on the sheet:
  //   Entradas de Tiempo
  //   Contador de Ciclos del Reloj
endmodule

module CONTROL_UNIT (
  input  Este_bit_me_lo_pasa_el_instruction_decoder,
  input  Reloj,
  input  Start,
  input  Reset,
  input  [1:0] operacion,
  input  [3:0] Read_Time,
  input  [3:0] Write_Time,
  output SET_SP,
  output Load_Info
);

  wire d_ff_1_q, demultiplexer_1_out0, demultiplexer_1_out1, demultiplexer_2_out0, demultiplexer_2_out1,
       Insruction_Read_q, Leer, Load_PC0, not_1_out, or_1_out, or_2_out, or_3_out, R_W_RF0, SET_SP_q;
  wire [31:0] counter_1_q;

  D_Flip_Flop d_ff_1 (.clk(Reloj), .D(demultiplexer_1_out0), .Q(d_ff_1_q), .preset(not_1_out));  // open: Qn, en, reset
  not not_1 (not_1_out, Start);
  buf or_1 (or_1_out, d_ff_1_q);  // OR_Gate
  Demultiplexer #(.enable("false")) demultiplexer_1 (
    .out0(demultiplexer_1_out0), .out1(demultiplexer_1_out1), .in(or_1_out), .sel(Start));
  or or_2 (or_2_out, SET_SP_q, demultiplexer_1_out1);
  Counter #(.width(32), .max('hffffffff)) counter_1 (
    .Q(counter_1_q), .clk(or_2_out), .clr(Reset));  // open: load, D, count, carry
  D_Flip_Flop #(.trigger("falling")) u_SET_SP (
    .clk(Reloj), .D(demultiplexer_1_out1), .Q(SET_SP_q));  // open: Qn, preset, en, reset
  Comparator #(.width(32)) comparator_1 (.a(counter_1_q), .b(32'h1), .eq(SET_SP));  // open: gt, lt
  D_Flip_Flop #(.trigger("falling")) Insruction_Read (
    .clk(Reloj), .D(or_3_out), .Q(Insruction_Read_q), .reset(Reset));  // open: Qn, preset, en
  or or_3 (or_3_out, SET_SP_q, demultiplexer_2_out0);
  Contador_de_Ciclos contador_de_ciclos_1 (
    .Read_Time(Read_Time), .Write_Time(Write_Time), .Reloj(Reloj),
    .R_W(Este_bit_me_lo_pasa_el_instruction_decoder), .Leido(Leer));  // open: Escrito
  Demultiplexer #(.enable("false")) demultiplexer_2 (
    .out0(demultiplexer_2_out0), .out1(demultiplexer_2_out1), .in(Insruction_Read_q), .sel(Leer));
  D_Flip_Flop #(.trigger("falling")) guardar_ifo (
    .clk(Reloj), .D(demultiplexer_2_out1), .Q(Load_Info));  // open: Qn, preset, en, reset
  Demultiplexer #(.select(2), .enable("false")) demultiplexer_3 (
    .out0(Load_PC0), .out1(R_W_RF0), .in(Load_Info), .sel(operacion));  // open: out2, out3

  // Other names for the same wires on the sheet: CLK = Reloj; Op[1:0] = operacion; Read_Tm[3:0] = Read_Time;
  //   Resert = Reset; Write_Tm[3:0] = Write_Time

  // Notes on the sheet:
  //   Start: pull=down
  //   Reloj
  //   Selector de Operacion
  //   INDLE
  //   ACTIVAR EL SET SP solo una vez al iniciar el programa 
  //   (se lo pasa el instruction Decoder)
  //   Control Unit
  //   Cargar info de la RAM
  //   Contador de ciclos
  //   paraa guardar la informacion que vino de la ram 
  //   Jmp, nor, Jr
  //   Alu (Tipo R and Tipo I)
endmodule
