// Logisim project InstructionDecoder.circ as structural Verilog
module InstructionDecoder (
  input  [5:0] OP_Code,
  output R,
  output I,
  output J
);

  wire and_1_out, and_2_out, and_4_out, and_5_out, and_6_out, and_7_out, and_8_out, and_9_out, and_10_out,
       and_11_out, and_12_out, and_13_out, and_14_out, and_15_out, and_16_out, and_17_out, and_18_out,
       and_19_out, and_20_out, and_21_out, and_22_out;

  and and_1 (and_1_out, ~OP_Code[0], OP_Code[1], ~OP_Code[2]);  // AND_Gate
  and and_2 (and_2_out, ~OP_Code[3], ~OP_Code[4], ~OP_Code[5]);  // AND_Gate
  and and_3 (J, and_1_out, and_2_out);
  and and_4 (and_4_out, ~OP_Code[4], ~OP_Code[5]);  // AND_Gate
  and and_5 (and_5_out, ~OP_Code[4], OP_Code[5]);  // AND_Gate
  and and_6 (and_6_out, ~OP_Code[0], ~OP_Code[2], OP_Code[3]);  // AND_Gate
  and and_7 (and_7_out, ~OP_Code[0], ~OP_Code[1], OP_Code[2]);  // AND_Gate
  and and_8 (and_8_out, OP_Code[1], OP_Code[2], ~OP_Code[3]);  // AND_Gate
  and and_9 (and_9_out, OP_Code[0], ~OP_Code[1], ~OP_Code[3]);  // AND_Gate
  and and_10 (and_10_out, OP_Code[0], OP_Code[1], ~OP_Code[2]);  // AND_Gate
  and and_11 (and_11_out, and_6_out, and_4_out);
  and and_12 (and_12_out, and_7_out, and_4_out);
  and and_13 (and_13_out, and_8_out, and_4_out);
  and and_14 (and_14_out, and_9_out, and_4_out);
  and and_15 (and_15_out, and_10_out, and_5_out);
  and and_16 (and_16_out, OP_Code[0], OP_Code[1], OP_Code[2], OP_Code[3], OP_Code[4], OP_Code[5]);
  and and_17 (and_17_out, ~OP_Code[0], ~OP_Code[1], ~OP_Code[2]);  // AND_Gate
  and and_18 (and_18_out, OP_Code[3], OP_Code[4], OP_Code[5]);
  and and_19 (and_19_out, ~OP_Code[0], ~OP_Code[1], ~OP_Code[2]);  // AND_Gate
  and and_20 (and_20_out, ~OP_Code[3], ~OP_Code[4], ~OP_Code[5]);  // AND_Gate
  and and_21 (and_21_out, and_17_out, and_18_out);
  and and_22 (and_22_out, and_19_out, and_20_out);
  or or_1 (I, and_11_out, and_12_out, and_13_out, and_14_out, and_15_out);
  or or_2 (R, and_16_out, and_21_out, and_22_out);

  // Other names for the same wires on the sheet: B0 = OP_Code[0]; B1 = OP_Code[1]; B2 = OP_Code[2]; B3 = OP_Code[3];
  //   B4 = OP_Code[4]; B5 = OP_Code[5]

  // Notes on the sheet:
  //   OP-Code TIPO J
  //   OP-Code TIPO I
  //   OP-Code TIPO R
endmodule
